# Fritzing sketch spectrometer_wiring_arduino (saved by Fritzing 0.8.7b)
breadboards: 1

parts:
  R1 = Resistor [tolerance=±5% resistance=220 package=THT]
  R2 = Resistor [tolerance=±5% resistance=220 package=THT]
  Part1 = Arduino Uno (Rev3) - ICSP
  X1 = DB9 Connector [package=db9]
  X2 = DB9 Connector [package=db9]
  L298N1 = L298N DC motor driver
  S1 = Pushbutton [package="[THT]"]  # not connected
  S2 = Pushbutton [package="[THT]"]  # not connected
  S3 = Pushbutton [package="[THT]"]  # not connected
  S4 = Pushbutton [package="[THT]"]  # not connected
  S5 = Pushbutton [package="[THT]"]  # not connected
  S6 = Pushbutton [package="[THT]"]  # not connected
  LCD1 = LCD screen
  S7 = SWITCH-MOMENTARY-2 [package=tactile-switch-1101ne]
  S8 = SWITCH-MOMENTARY-2 [package=tactile-switch-1101ne]
  M1 = Stepper Motor - Bipolar
  R3 = TRIMPOT [package=trimpot_pth_s3_lock]
  J1 = Power Jack [package=power_jack_pth_lock]
  R4 = Resistor [tolerance=±5% resistance=220 package=THT]

nets:
  5V: R1.Pin_0, R2.Pin_0, Part1.5V, L298N1.5V
  N1: R1.Pin_1, R2.Pin_1, Part1.D2, X1.6, X1.8
  N2: Part1.D8, LCD1.RS
  N3: Part1.D9_PWM, LCD1.E
  N4: Part1.D10_PWM/SS, L298N1.IN1
  N5: Part1.D11_PWM/MOSI, L298N1.IN2
  N6: Part1.D12/MISO, L298N1.IN3
  N7: Part1.D13/SCK, L298N1.IN4
  N8: Part1.D3_PWM, L298N1.ENA, L298N1.ENB
  N9: Part1.D4, LCD1.DB4
  N10: Part1.D5_PWM, LCD1.DB5
  N11: Part1.D6_PWM, LCD1.DB6
  N12: Part1.D7, LCD1.DB7
  GND: Part1.GND, X1.7, L298N1.GND, LCD1.VSS, LCD1.R/W, LCD1.LED-, R3.CW, J1.GND
  N13: X1.1, L298N1.OUT1
  N14: X1.2, L298N1.OUT2
  N15: X1.3, L298N1.OUT3
  N16: X1.4, L298N1.OUT4
  N17: X2.1, M1.D
  N18: X2.2, M1.B
  N19: X2.3, M1.C
  N20: X2.4, M1.A
  N21: X2.6, S7.1
  N22: X2.7, S7.2, S8.1
  N23: X2.8, S8.2
  N24: L298N1.12V, J1.GNDBREAK
  N25: LCD1.VDD, R3.CCW
  N26: LCD1.V0, R3.WIPER
  N27: LCD1.LED+, R4.Pin_1

custom parts:
  L298N DC motor driver: 2x DC motor driver with 78M05 positive voltage regulator (7..35 V) L298N: max 46 V, 2 A Set 5 V Enable jumper to enable 5 V regultor (needed for the L298N) and +5 V output at screw terminal or supply external +5 V at screw terminal Set ENA and/or ENB to +5 V to enable motor permanently or supply ENA and/or ENB with PWM signal IN1 and IN2 set rotation directory for motor A (OUT1/OUT2) IN2 and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
